# Fritzing sketch facetracker (saved by Fritzing 0.9.2b)
breadboards: 1

parts:
  Part1 = RedBear-Duo
  LED1 = LED - 5mm [color="Red (633nm)" package="5 mm [THT]"]  # not connected
  J1 = Piezo Speaker
  Part2 = SRF05 Ultrasonic Rangefinder
  J2 = Basic Servo
  R1 = Resistor [tolerance=±5% resistance=220 package=THT]  # not connected

nets:
  N1: Part1.A0, J1.pin2
  GND: Part1.GND, J1.pin1, Part2.GND, J2.gnd
  N2: Part1.D0, Part2.Trig
  N3: Part1.D1, Part2.Echo
  N4: Part1.D3, J2.pulse
  VCC: Part1.3V3, Part2.VCC, J2.vcc

custom parts:
  RedBear-Duo: Duo is a thumb-size development board made to simplify the building process of Internet of Things (IoT). This part is a modification of the Particle Photon part by Brett Walach,Fabian Althaus
